# Fritzing sketch Plasma Board (saved by Fritzing 0.9.3b)
circuit board: 9.37785cm x 12.2556cm
breadboards: 1

parts:
  J1 = shrouded pin header, 40 pins [form="♂ (shrouded male)"]
  J5 = Generic female header - 2 pins [form="♀ (female)" package=THT]
  J6 = Generic female header - 2 pins [form="♀ (female)" package=THT]
  J7 = Generic female header - 2 pins [form="♀ (female)" package=THT]
  J4 = Generic female header - 2 pins [form="♀ (female)" package=THT]
  R1 = Resistor [tolerance=±5% resistance=220 package=THT]
  R2 = Resistor [tolerance=±5% resistance=220 package=THT]
  R3 = Resistor [tolerance=±5% resistance=220 package=THT]
  R4 = Resistor [tolerance=±5% resistance=220 package=THT]
  J2 = shrouded pin header, 10 pins [form="♂ (shrouded male)"]
  J9 = shrouded pin header, 40 pins [form="♂ (shrouded male)"]
  J8 = molex pin header, 2 pins [form=molex]
  OMRON1 = OMRON PCB Power Relay – G5LE [part_number="G5LE-1\n" package=THT]
  J10 = molex pin header, 2 pins [form=molex]  # not connected
  J12 = molex pin header, 4 pins [form=molex]
  J13 = male pin header, 2 pins [form="♂ (male)"]  # not connected
  J14 = male pin header, 2 pins [form="♂ (male)"]  # not connected
  WeMos_D1_Mini_Micro_SD_Shield1 = WeMos D1 Mini Micro SD Shield  # not connected
  Q1 = NPN-Transistor [package="TO92 [THT]"]
  R5 = Resistor [tolerance=±5% resistance=220 package=THT]
  J15 = male pin header, 3 pins [form="♂ (male)"]
  J16 = male pin header, 3 pins [form="♂ (male)"]
  D1 = Zener Diode [part_number=1N4732A breakdown_voltage=3.6V package="300 mil [THT]"]

nets:
  N1: J1.pin1, J1.pin40, J4.pin2, J4.pin_11
  N2: J1.pin2, J1.pin39, J4.pin_3, J4.pin_10
  N3: J1.pin3, J1.pin38, J4.pin_4, J4.pin_9
  N4: J1.pin4, J1.pin37, J4.pin_5, J4.pin_8
  N5: J1.pin5, J1.pin36, J6.pin2, J6.pin_11
  N6: J1.pin6, J1.pin35, J6.pin_3, J6.pin_10
  N7: J1.pin7, J1.pin34, J6.pin_4, J6.pin_9
  N8: J1.pin8, J1.pin33, J6.pin_5, J6.pin_8
  N9: J1.pin9, J1.pin32, J7.pin2, J7.pin_11
  N10: J1.pin10, J1.pin31, J7.pin_3, J7.pin_10
  N11: J1.pin11, J1.pin30, J7.pin_4, J7.pin_9
  N12: J1.pin12, J1.pin29, J7.pin_5, J7.pin_8
  N13: J1.pin13, J1.pin28, J5.pin2, J5.pin_11
  N14: J1.pin14, J1.pin27, J5.pin_3, J5.pin_10
  N15: J1.pin15, J1.pin26, J5.pin_4, J5.pin_9
  N16: J1.pin16, J1.pin25, J5.pin_5, J5.pin_8
  N17: J1.pin17, J1.pin19, J1.pin21, J1.pin23, J5.pin_17, J6.pin_17, J7.pin_17, J4.pin_17, J2.pin2, OMRON1.COIL1, D1.cathode
  N18: J1.pin18, R1.Pin_1
  N19: J1.pin20, R2.Pin_1
  N20: J1.pin22, R3.Pin_1
  N21: J1.pin24, R4.Pin_1
  N22: J5.pin1, J5.pin_12, J6.pin1, J6.pin_12, J7.pin1, J7.pin_12, J4.pin1, J4.pin_12, J8.pin2
  N23: J5.pin_6, J5.pin_7
  N24: J5.pin_14, J9.pin12
  N25: J5.pin_15, J9.pin11
  N26: J5.pin_16, J9.pin10
  N27: J5.pin_18, J6.pin_18, J7.pin_18, J4.pin_18
  N28: J5.pin_19, J6.pin_19, J7.pin_19, J4.pin_19
  N29: J5.pin_20, J6.pin_20, J7.pin_20, J4.pin_20
  N30: J6.pin_6, J6.pin_7
  N31: J6.pin_14, J7.pin_14, J9.pin15
  N32: J6.pin_15, J7.pin_15, J9.pin14
  N33: J6.pin_16, J7.pin_16, J9.pin13
  N34: J7.pin_6, J7.pin_7
  N35: J4.pin_6, J4.pin_7
  N36: J4.pin_14, J9.pin18
  N37: J4.pin_15, J9.pin17
  N38: J4.pin_16, J9.pin16
  N39: R1.Pin_0, R2.Pin_0, R3.Pin_0, R4.Pin_0, J2.pin1
  N40: J2.pin5, J16.pin1
  N41: J2.pin6, J15.pin1
  N42: OMRON1.COIL2, Q1.C, D1.anode
  N43: J12.pin1, J16.pin3
  N44: J12.pin2, J15.pin3
  N45: Q1.B, R5.Pin_0

notes:
  X
  Y2
  Y1
  Z
  24v In
  Machine Connection
  Arduino
  Torch Height Control
  -
  +
  GND
  EN/CS
  STEP
  DIR
  +VCC
  +VMOT
  Driver
  2211
  Dir
  Step
  D ->
  S ->
  D <-
  S <-

custom parts:
  Generic female header - 2 pins: Generic female header
